# Fritzing sketch sensor_alarm_clock_with_temp_&_humid_lcd_v.1.0 (saved by Fritzing 0.9.6b)
breadboards: 2

parts:
  Part1 = Arduino Uno (Rev3) - ICSP
  S1 = Pushbutton [package="[SMD]"]
  R1 = Resistor [tolerance=±5% power=0.25 resistance=10k package=THT]
  S2 = Pushbutton [package="[SMD]"]
  R2 = Resistor [tolerance=±5% power=0.25 resistance=10k package=THT]
  S3 = Pushbutton [package="[SMD]"]
  R3 = Resistor [tolerance=±5% power=0.25 resistance=10k package=THT]
  ZS-042_RTC1 = ZS-042 RTC Module  # not connected
  R4 = Rotary Potentiometer (Small) [maximum_resistance=100kΩ package=THT]
  LCD1 = LCD screen
  J1 = Piezo Speaker
  Mod1 = KY-015 Temperature & Humidity Sensor Module [package="Breakout board"]
  part = HC-SR501 Body Sensor Module
  LED1 = smd LED [color="Red (633nm)" package="1206 [SMD]"]
  LED2 = smd LED [color="Green (560nm)" package="1206 [SMD]"]
  R5 = Resistor [tolerance=±5% power=0.25 resistance=10k package=THT]
  R6 = Resistor [tolerance=±5% power=0.25 resistance=10k package=THT]
  R7 = Resistor [tolerance=±5% power=0.25 resistance=10k package=THT]

nets:
  N1: Part1.A0, part.OUT
  N2: Part1.A1, S1.Pin_1, S1.Pin_2, R1.Pin_0
  N3: Part1.A2, S2.Pin_1, S2.Pin_2, R2.Pin_0
  N4: Part1.A3, S3.Pin_1, S3.Pin_2, R3.Pin_0
  N5: Part1.D8, R6.Pin_0
  N6: Part1.D9_PWM, R7.Pin_0
  N7: Part1.D10_PWM/SS, J1.pin2
  N8: Part1.D11_PWM/MOSI, LCD1.E
  N9: Part1.D12/MISO, LCD1.RS
  N10: Part1.D2, LCD1.DB7
  N11: Part1.D3_PWM, LCD1.DB6
  N12: Part1.D4, LCD1.DB5
  N13: Part1.D5_PWM, LCD1.DB4
  N14: Part1.D6_PWM, Mod1.Vin
  N15: Part1.GND, S1.Pin_3, S1.Pin_4, S2.Pin_3, S2.Pin_4, S3.Pin_3, S3.Pin_4
  VSS: R1.Pin_1, R3.Pin_1, R4.leg1, LCD1.VSS, LCD1.R/W, LCD1.LED-, J1.pin1, part.GND, LED2.cathode
  N16: R4.wiper, LCD1.V0
  VDD: R4.leg2, LCD1.VDD, part.VCC, R5.Pin_1
  N17: LCD1.LED+, R5.Pin_0
  N18: Mod1.S, LED1.cathode
  N19: LED1.anode, R7.Pin_1
  N20: LED2.anode, R6.Pin_1

custom parts:
  KY-015 Temperature & Humidity Sensor Module: KY-015 temperature and humidity sensor module, provides a low-latency serial interface to measure humidity and temperature.
  HC-SR501 Body Sensor Module: Pyroelectric Infrared PIR Motion Sensor Detector Module
